# Fritzing sketch arm (saved by Fritzing 0.7.12b)
breadboards: 1

parts:
  LCD1 = LCD screen
  ENCODER2 = Rotary Encoder with Knob
  ENCODER3 = Rotary Encoder with Knob
  ENCODER4 = Rotary Encoder with Knob
  S1 = Toggle Switch [package=THT]
  J1 = female pin header, 15 pins [form="♀ (female)"]
  ENCODER1 = Rotary Encoder with Knob

nets:
  N1: LCD1.VSS, LCD1.V0, LCD1.DB0, LCD1.DB1, ENCODER2.no_name_yet#2, ENCODER2.no_name_yet#4, ENCODER3.no_name_yet#2, ENCODER3.no_name_yet#4, ENCODER4.no_name_yet#2, S1.L2, J1.pin1, ENCODER1.no_name_yet#2, ENCODER1.no_name_yet#4
  N2: LCD1.VDD, J1.pin2
  N3: LCD1.RS, J1.pin3
  N4: LCD1.R/W, J1.pin4
  N5: ENCODER2.no_name_yet#1, J1.pin13
  N6: ENCODER2.no_name_yet#3, J1.pin12
  N7: ENCODER2.no_name_yet#5, J1.pin7
  N8: ENCODER3.no_name_yet#1, J1.pin11
  N9: ENCODER3.no_name_yet#3, J1.pin10
  N10: ENCODER4.no_name_yet#1, J1.pin9
  N11: ENCODER4.no_name_yet#3, J1.pin8
  N12: S1.COM, J1.pin5
  N13: J1.pin6, ENCODER1.no_name_yet#5
  N14: J1.pin14, ENCODER1.no_name_yet#3
  N15: J1.pin15, ENCODER1.no_name_yet#1

custom parts:
  Rotary Encoder with Knob: Rotary Encoder with 1/4" Shaft and Knob
