# Fritzing sketch teensy (saved by Fritzing 0.7.12b)
breadboards: 1

parts:
  Teensy_3_1 = Teensy 3.0 [part_number="Freescale ARM MK20DX128"]
  U1 = mystery part, 20 pins [chip_label=?]
  R2 = Resistor [tolerance=±5% resistance=220 package=THT]
  R3 = Resistor [tolerance=±5% resistance=220 package=THT]
  R1 = Resistor [tolerance=±5% resistance=220 package=THT]
  R4 = Resistor [tolerance=±5% resistance=220 package=THT]
  R5 = Resistor [tolerance=±5% resistance=220 package=THT]
  R6 = Resistor [tolerance=±5% resistance=220 package=THT]
  R7 = Resistor [tolerance=±5% resistance=220 package=THT]
  R8 = Resistor [tolerance=±5% resistance=220 package=THT]
  J1 = screw terminal, 8 pins  # not connected
  J12 = screw terminal, 8 pins  # not connected

nets:
  N1: Teensy_3_1.21, U1.pin19
  N2: Teensy_3_1.20, U1.pin18
  N3: Teensy_3_1.16, Teensy_3_1.15
  N4: Teensy_3_1.14, U1.pin17
  N5: Teensy_3_1.1, U1.pin12
  N6: Teensy_3_1.5, U1.pin13
  N7: Teensy_3_1.6, U1.pin14
  N8: Teensy_3_1.7, U1.pin15
  N9: Teensy_3_1.8, U1.pin16
  N10: U1.pin1, R7.Pin_1
  N11: U1.pin2, R8.Pin_1
  N12: U1.pin3, R6.Pin_1
  N13: U1.pin4, R5.Pin_1
  N14: U1.pin5, R4.Pin_1
  N15: U1.pin6, R3.Pin_1
  N16: U1.pin7, R1.Pin_1
  N17: U1.pin8, R2.Pin_1
