# Fritzing sketch teensy2 (saved by Fritzing 0.7.12b)
breadboards: 1

parts:
  J3 = screw terminal, 4 pins
  J5 = screw terminal, 3 pins
  J7 = screw terminal, 3 pins
  J8 = screw terminal, 3 pins
  J10 = screw terminal, 3 pins
  J12 = screw terminal, 3 pins
  R13 = Resistor [tolerance=±5% resistance=220 package=THT]
  R10 = Resistor [tolerance=±5% resistance=220 package=THT]
  R12 = Resistor [tolerance=±5% resistance=220 package=THT]
  R11 = Resistor [tolerance=±5% resistance=220 package=THT]
  R15 = Resistor [tolerance=±5% resistance=220 package=THT]
  R16 = Resistor [tolerance=±5% resistance=220 package=THT]
  R9 = Resistor [tolerance=±5% resistance=220 package=THT]
  R14 = Resistor [tolerance=±5% resistance=220 package=THT]
  U3 = mystery part, 28 pins [chip_label=?]
  U6 = mystery part, 10 pins [chip_label=?]
  U4 = mystery part, 10 pins [chip_label=?]
  U9 = mystery part, 8 pins [chip_label=?]
  tx = mystery part, 3 pins [chip_label=tx]
  Audio = mystery part, 3 pins [chip_label=tx]
  U2 = mystery part, 20 pins [chip_label=?]
  U5 = mystery part, 14 pins [chip_label=?]
  J6 = Screw terminal - 2 pins [package=THT]
  J11 = screw terminal, 3 pins
  LCD2 = LCD screen
  ENCODER5 = Rotary Encoder with Knob
  ENCODER6 = Rotary Encoder with Knob
  ENCODER7 = Rotary Encoder with Knob
  ENCODER8 = Rotary Encoder with Knob
  J13 = female pin header, 15 pins [form="♀ (female)"]
  Pad1 = Pad [width=9.15598820058993 height=2.91712881022616 connect=center]
  Pad2 = Pad [width=9.15598820058993 height=2.91712881022616 connect=center]

nets:
  N1: J3.pin1, U6.pin7
  N2: J3.pin2, U6.pin6
  N3: J3.pin3, J5.pin2, J7.pin2, J8.pin2, J10.pin2, J12.pin2, U6.pin2, J6.pin1, J11.pin2
  N4: J3.pin4, J5.pin3, J7.pin3, J8.pin3, J10.pin3, J12.pin3, U6.pin1, J6.pin2, J11.pin1
  N5: J5.pin1, U6.pin10
  N6: J7.pin1, U6.pin3
  N7: J8.pin1, U6.pin9
  N8: J10.pin1, U6.pin5
  N9: J12.pin1, U6.pin4
  N10: R13.Pin_0, U4.pin7
  N11: R13.Pin_1, U2.pin2
  N12: R10.Pin_0, U4.pin8
  N13: R10.Pin_1, U2.pin1
  N14: R12.Pin_0, U4.pin6
  N15: R12.Pin_1, U2.pin3
  N16: R11.Pin_0, U4.pin5
  N17: R11.Pin_1, U2.pin4
  N18: R15.Pin_0, U4.pin4
  N19: R15.Pin_1, U2.pin5
  N20: R16.Pin_0, U4.pin3
  N21: R16.Pin_1, U2.pin6
  N22: R9.Pin_0, U4.pin1
  N23: R9.Pin_1, U2.pin7
  N24: R14.Pin_0, U4.pin2
  N25: R14.Pin_1, U2.pin8
  N26: U3.pin1, U4.pin9, U9.pin2, U9.pin7, tx.pin3, U2.pin9, U2.pin20, U5.pin13
  N27: U3.pin2, tx.pin1
  N28: U3.pin3, U5.pin11
  N29: U3.pin4, U2.pin15
  N30: U3.pin5, U5.pin10
  N31: U3.pin6, U5.pin9
  N32: U3.pin7, U2.pin16
  N33: U3.pin8, U2.pin17
  N34: U3.pin9, U2.pin18
  N35: U3.pin10, U2.pin19
  N36: U3.pin11, U5.pin8
  N37: U3.pin12, U5.pin7
  N38: U3.pin13, U5.pin6
  N39: U3.pin14, U5.pin5
  N40: U3.pin15, U5.pin4
  N41: U3.pin16, U2.pin12
  N42: U3.pin17, U3.pin18
  N43: U3.pin19, U5.pin3
  N44: U3.pin20, U9.pin6
  N45: U3.pin21, U9.pin5
  N46: U3.pin22, U2.pin13
  N47: U3.pin23, U2.pin14
  N48: U3.pin24, Audio.pin3
  N49: U3.pin25, U5.pin12
  N50: U3.pin26, U9.pin8, tx.pin2, Audio.pin2
  N51: U3.pin27, Audio.pin1
  N52: U3.pin28, U4.pin10, U9.pin1, U2.pin10, U2.pin11, U5.pin14
  N53: U6.pin8, J11.pin3
  N54: U9.pin3, U5.pin2
  N55: U9.pin4, U5.pin1
  N56: LCD2.VSS, LCD2.DB0, ENCODER5.no_name_yet#2, ENCODER6.no_name_yet#2, ENCODER7.no_name_yet#2, ENCODER8.no_name_yet#2, J13.pin1, Pad2.pad
  N57: LCD2.VDD, LCD2.V0, LCD2.DB1, J13.pin2
  N58: LCD2.RS, J13.pin3
  N59: LCD2.R/W, J13.pin4
  N60: ENCODER5.no_name_yet#1, J13.pin15
  N61: ENCODER5.no_name_yet#3, J13.pin14
  N62: ENCODER5.no_name_yet#4, ENCODER8.no_name_yet#4
  N63: ENCODER5.no_name_yet#5, J13.pin6
  N64: ENCODER6.no_name_yet#1, J13.pin9
  N65: ENCODER6.no_name_yet#3, J13.pin8
  N66: ENCODER7.no_name_yet#1, J13.pin11
  N67: ENCODER7.no_name_yet#3, J13.pin10
  N68: ENCODER8.no_name_yet#1, J13.pin13
  N69: ENCODER8.no_name_yet#3, J13.pin12
  N70: ENCODER8.no_name_yet#5, J13.pin7
  N71: J13.pin5, Pad1.pad

notes:
  GND
  5v
  3v

custom parts:
  Rotary Encoder with Knob: Rotary Encoder with 1/4" Shaft and Knob
